# Fritzing sketch Schema (saved by Fritzing 1.0.1rc)
breadboards: 1

parts:
  SparkFun_ESP32_Thing1 = SparkFun ESP32 Thing [part_number=DEV-13907]
  VCC1 = Battery block 9V
  Composant2 = Adafruit I2S Mic - SPH0645 [part_number="Adafruit #3421"]
  A1 = Waveshare e-Paper HAT with 7in display [package=THT]

nets:
  GND: SparkFun_ESP32_Thing1.GND, VCC1.-, Composant2.GND, Composant2.SELECT, A1.pin_7
  3.3V: SparkFun_ESP32_Thing1.3.3V, VCC1.+, Composant2.VDD, A1.pin_8
  N1: SparkFun_ESP32_Thing1.26, Composant2.BCLK
  N2: SparkFun_ESP32_Thing1.16, A1.pin_2
  N3: SparkFun_ESP32_Thing1.17, A1.pin_3
  N4: SparkFun_ESP32_Thing1.4, A1.pin_1
  N5: SparkFun_ESP32_Thing1.5, A1.pin_4
  N6: SparkFun_ESP32_Thing1.18, A1.pin_5
  N7: SparkFun_ESP32_Thing1.23, A1.pin_6
  N8: SparkFun_ESP32_Thing1.22, Composant2.WS
  N9: SparkFun_ESP32_Thing1.21, Composant2.DATA

custom parts:
  SparkFun ESP32 Thing: The SparkFun ESP32 Thing is a comprehensive development platform for Espressif’s ESP32, their super-charged version of the popular ESP8266. Like the 8266, the ESP32 is a WiFi-compatible microcontroller, but to that it adds support for Bluetooth low-energy (i.e BLE, BT4.0, Bluetooth Smart), and nearly 30 I/O pins. The ESP32’s power and versatility will make it the foundation of IoT and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
  Adafruit I2S Mic - SPH0645: For many microcontrollers, adding audio input is easy with one of our analog microphone breakouts. But as you get to bigger and better microcontrollers and microcomputers, you'll find that you don't always have an analog input, or maybe you want to avoid the noise that can seep in with an analog mic system. Once you get past 8-bit micros, you will often find an I2S peripheral, that can take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
  Waveshare e-Paper HAT with 7in display: .This is a universal driver board for e-Paper raw panels, can be used to drive various SPI interface e-Paper from Waveshare. This version includes a 7in display panel in breadboard.
